# Fritzing sketch 10_DCmotor-Anuduino (saved by Fritzing 0.8.7b)
breadboards: 1

parts:
  M1 = DC Motor
  Q1 = TRANSISTOR_NPN [package=to-92-ammo]
  VCC1 = 4 x AAA Battery Mount
  R1 = Resistor [tolerance=±5% resistance=220 package=THT]
  D1 = Rectifier Diode [part_number=1N4001 package="300 mil [THT]"]
  U1 = attiny85 [package=dip]

nets:
  N1: M1.pin_1, VCC1.-, D1.cathode, U1.Pin_8
  N2: M1.pin_2, Q1.E, D1.anode
  N3: Q1.B, R1.Pin_1
  N4: Q1.C, VCC1.+, U1.Pin_4
  N5: R1.Pin_0, U1.Pin_5

custom parts:
  4 x AAA Battery Mount: A 4 x AAA battery pack (4.8 Volts with recharables)
