# Fritzing sketch 11_Two-DCmotors (saved by Fritzing 0.8.7b)
breadboards: 1

parts:
  R1 = Resistor [tolerance=±5% resistance=220 package=THT]
  R2 = Resistor [tolerance=±5% resistance=220 package=THT]
  M1 = DC Motor
  M2 = DC Motor
  D1 = Rectifier Diode [part_number=1N4001 package="300 mil [THT]"]
  D2 = Rectifier Diode [part_number=1N4001 package="300 mil [THT]"]
  U1 = attiny85 [package=dip]
  VCC1 = 4 x AAA Battery Mount
  Q1 = NPN-Transistor [package="TO92 [THT]"]
  Q2 = NPN-Transistor [package="TO92 [THT]"]

nets:
  N1: R1.Pin_0, U1.Pin_5
  N2: R1.Pin_1, Q2.B
  N3: R2.Pin_0, U1.Pin_6
  N4: R2.Pin_1, Q1.B
  N5: M1.pin_1, M2.pin_2, D1.cathode, D2.cathode, U1.Pin_8, VCC1.-
  N6: M1.pin_2, D1.anode, Q2.E
  N7: M2.pin_1, D2.anode, Q1.C
  N8: U1.Pin_4, VCC1.+, Q1.E, Q2.C

custom parts:
  4 x AAA Battery Mount: A 4 x AAA battery pack (4.8 Volts with recharables)
