# Fritzing sketch 12_Relay-Anuduino (saved by Fritzing 0.8.7b)
breadboards: 1

parts:
  U1 = attiny85 [package=dip]
  U2 = RELAY [package=relay-t9a]
  D1 = Rectifier Diode [part_number=1N4001 package="300 mil [THT]"]
  R1 = Resistor [tolerance=±5% resistance=2.2k package=THT]
  R2 = Resistor [tolerance=±10% resistance=470 package=THT]  # not connected
  Q1 = NPN-Transistor [package="TO92 [THT]"]
  LED1 = LED - 5mm [color="Red (633nm)" package="5 mm [THT]"]  # not connected

nets:
  N1: U1.Pin_4, Q1.E
  N2: U1.Pin_6, R1.Pin_0
  N3: U2.COIL1, D1.anode, Q1.C
  N4: U2.COIL2, D1.cathode
  N5: R1.Pin_1, Q1.B
