# Fritzing sketch 13_Halleffect_sensor (saved by Fritzing 0.8.7b)
breadboards: 1

parts:
  44E_317 = HALL-EFFECT [package=sc70]
  LED1 = LED - 5mm [color="Red (633nm)" package="5 mm [THT]"]
  R1 = Resistor [tolerance=±5% resistance=220 package=THT]
  R2 = Resistor [tolerance=±5% resistance=220 package=THT]
  VCC1 = 4 x AAA Battery Mount
  U3 = attiny85 [package=dip]

nets:
  N1: 44E_317.GND, LED1.anode, VCC1.+, U3.Pin_4
  N2: 44E_317.VCC, R1.Pin_0, VCC1.-, U3.Pin_8
  N3: 44E_317.OUT, R1.Pin_1, U3.Pin_6
  N4: LED1.cathode, R2.Pin_1
  N5: R2.Pin_0, U3.Pin_5

custom parts:
  4 x AAA Battery Mount: A 4 x AAA battery pack (4.8 Volts with recharables)
