# Fritzing sketch 14_Thermistor-Anuduino (saved by Fritzing 0.8.7b)
breadboards: 1

parts:
  U1 = attiny85 [package=dip]
  USB = USB connector [package=THT]
  R1 = Resistor [tolerance=±5% resistance=1.5k package=THT]
  D1 = Zener Diode [part_number=1N4732A breakdown_voltage=3.6V package="300 mil [THT]"]
  R2 = Resistor [tolerance=±5% resistance=68 package=THT]
  R3 = Resistor [tolerance=±5% resistance=68 package=THT]
  R4 = Temperature Sensor (Thermistor) [thermistor_type=NTC package=THT]
  R5 = Resistor [tolerance=±5% resistance=10k package=THT]
  D2 = Zener Diode [part_number=1N4732A breakdown_voltage=3.6V package="Melf DO-213 AB [SMD]"]

nets:
  N1: U1.Pin_2, R2.Pin_1
  N2: U1.Pin_3, R3.Pin_1
  N3: U1.Pin_4, USB.GND, USB.chassis5, USB.chassis6, D1.anode, R5.Pin_1, D2.anode
  N4: U1.Pin_7, R4.pin_1, R5.Pin_0
  N5: U1.Pin_8, USB.5V, R1.Pin_0, R4.pin_0
  N6: USB.d-, R1.Pin_1, R2.Pin_0, D2.cathode
  N7: USB.d+, D1.cathode, R3.Pin_0
