# Fritzing sketch 15_Humidity_sensor (saved by Fritzing 0.8.7b)
breadboards: 1

parts:
  CONN1 = USB connector [package=THT]
  U1 = attiny85 [package=dip]
  D1 = Zener Diode [part_number=1N4732A breakdown_voltage=3.6V package="Melf DO-213 AB [SMD]"]
  D2 = Zener Diode [part_number=1N4732A breakdown_voltage=3.6V package="Melf DO-213 AB [SMD]"]
  R1 = Resistor [tolerance=±5% resistance=68 package=THT]
  R2 = Resistor [tolerance=±5% resistance=68 package=THT]
  R3 = Resistor [tolerance=±5% resistance=1.5k package=THT]
  RHT1 = Humidity and Temperature Sensor RHT03
  R4 = Resistor [tolerance=±5% resistance=4.7k package=THT]

nets:
  5V: CONN1.5V, U1.Pin_8, R3.Pin_0, RHT1.Vcc
  N1: CONN1.d-, D1.cathode, R1.Pin_0, R3.Pin_1
  N2: CONN1.d+, D2.cathode, R2.Pin_0
  N3: CONN1.GND, CONN1.chassis5, CONN1.chassis6, U1.Pin_4, D1.anode, D2.anode, RHT1.GND_2, R4.Pin_1
  N4: U1.Pin_2, R1.Pin_1
  N5: U1.Pin_3, R2.Pin_1
  N6: U1.Pin_7, RHT1.Data-signal, R4.Pin_0
