# Fritzing sketch 16_IR-Anuduino (saved by Fritzing 0.8.7b)
breadboards: 1

parts:
  LED1 = LED - 3mm [color="Infrared (940nm)" package="3 mm [THT]"]
  U1 = attiny85 [package=dip]
  CONN1 = USB connector [package=THT]
  LED2 = LED - 3mm [color="Red (633nm)" package="3 mm [THT]"]
  LED3 = LED - 3mm [color="White (4500K)" package="3 mm [THT]"]
  R1 = Resistor [tolerance=±5% resistance=150 package=THT]
  R2 = Resistor [tolerance=±5% resistance=68 package=THT]
  R3 = Resistor [tolerance=±5% resistance=68 package=THT]
  R4 = Resistor [tolerance=±5% resistance=10k package=THT]
  D1 = Zener Diode [part_number=1N4732A breakdown_voltage=3.6V package="Melf DO-213 AB [SMD]"]
  D2 = Zener Diode [part_number=1N4732A breakdown_voltage=3.6V package="Melf DO-213 AB [SMD]"]
  R5 = Resistor [tolerance=±5% resistance=2.2k package=THT]

nets:
  N1: LED1.cathode, U1.Pin_8, CONN1.5V, R1.Pin_1, R5.Pin_0
  N2: LED1.anode, U1.Pin_7, LED2.anode, R4.Pin_0
  N3: U1.Pin_2, R2.Pin_1
  N4: U1.Pin_3, R3.Pin_1
  N5: U1.Pin_4, CONN1.GND, CONN1.chassis5, CONN1.chassis6, LED2.cathode, LED3.cathode, R4.Pin_1, D1.anode, D2.anode
  N6: CONN1.d-, R2.Pin_0, D1.cathode, R5.Pin_1
  N7: CONN1.d+, R3.Pin_0, D2.cathode
  N8: LED3.anode, R1.Pin_0
