# Fritzing sketch 17_Bluetooth (saved by Fritzing 0.8.7b)
breadboards: 1

parts:
  VCC1 = 4 x AAA Battery Mount
  U1 = attiny85 [package=dip]
  R1 = Resistor [tolerance=±5% resistance=470 package=THT]
  LED1 = LED - 5mm [color="Red (633nm)" package="5 mm [THT]"]
  HC-06 = Bluetooth Mate Silver
  VCC2 = Battery
  R2 = Resistor [tolerance=±5% resistance=50 package=THT]
  R3 = Resistor [tolerance=±5% resistance=100 package=THT]

nets:
  N1: VCC1.-, U1.Pin_4, R1.Pin_1, HC-06.GND, VCC2.-, R3.Pin_1
  N2: VCC1.+, U1.Pin_8
  N3: U1.Pin_2, LED1.anode
  N4: U1.Pin_5, HC-06.TX_5V
  N5: U1.Pin_6, R2.Pin_1
  N6: R1.Pin_0, LED1.cathode
  N7: HC-06.RX_5V, R2.Pin_0, R3.Pin_0
