# Fritzing sketch 18_zigbee_Receiver (saved by Fritzing 0.8.7b)
breadboards: 1

parts:
  LED1 = LED - 5mm [color="Red (633nm)" package="5 mm [THT]"]
  Part2 = XBee Explorer Regulated
  VCC1 = 4 x AAA Battery Mount  # not connected
  R1 = Resistor [tolerance=±5% resistance=10k package=THT]

nets:
  N1: LED1.cathode, R1.Pin_0
  N2: LED1.anode, Part2.DIO3
  N3: Part2.GND, R1.Pin_1
