# Fritzing sketch 18_zigbee_Transmittor (saved by Fritzing 0.8.7b)
breadboards: 1

parts:
  U1 = attiny85 [package=dip]
  VCC1 = 4 x AAA Battery Mount
  Part1 = XBee Explorer Regulated
  U2 = SWITCH_SPDT [package=kps-1290]

nets:
  N1: U1.Pin_4, VCC1.-, Part1.GND, U2.S
  N2: U1.Pin_5, Part1.DOUT
  N3: U1.Pin_6, Part1.DIN
  N4: U1.Pin_7, U2.P
  N5: U1.Pin_8, VCC1.+, Part1.5V, U2.O
