# Fritzing sketch 19_GPS (saved by Fritzing 0.8.7b)
breadboards: 1

parts:
  U1 = attiny85 [package=dip]
  U2 = SUP500F [package=sup500f]
  VCC1 = 4 x AAA Battery Mount

nets:
  N1: U1.Pin_4, U2.GND, VCC1.-
  N2: U1.Pin_5, U2.TX-O
  N3: U1.Pin_6, U2.RX-I
  N4: U1.Pin_8, U2.VCC, VCC1.+
