# Fritzing sketch 1_Blink_LED (saved by Fritzing 0.8.7b)
breadboards: 1

parts:
  R1 = Resistor [tolerance=±5% resistance=220 package=THT]
  U1 = attiny85 [package=dip]
  LED1 = LED - 5mm [color="Red (633nm)" package="5 mm [THT]"]
  VCC1 = prefix0000

nets:
  N1: R1.Pin_0, LED1.anode
  N2: R1.Pin_1, U1.Pin_6
  N3: U1.Pin_4, LED1.cathode, VCC1.connector0
  N4: U1.Pin_8, VCC1.connector1
