# Fritzing sketch 20_RFID (saved by Fritzing 0.8.7b)
breadboards: 1

parts:
  Part1 = RFID USB Reader
  VCC3 = Battery
  R4 = Resistor [tolerance=±5% resistance=50 package=THT]
  R5 = Resistor [tolerance=±5% resistance=100 package=THT]
  VCC4 = 4 x AAA Battery Mount
  HC-7 = Bluetooth Mate Silver
  U2 = attiny85 [package=dip]

nets:
  N1: Part1.TX-O, U2.Pin_7
  GND: Part1.GND, VCC3.-, R5.Pin_1, VCC4.-, HC-7.GND, U2.Pin_4
  N2: Part1.VCC, VCC4.+, U2.Pin_8
  N3: R4.Pin_0, R5.Pin_0, HC-7.RX_5V
  N4: R4.Pin_1, U2.Pin_6
