# Fritzing sketch 21_GSM (saved by Fritzing 0.8.7b)
breadboards: 1

parts:
  U1 = attiny85 [package=dip]  # not connected
  Part1 = Arduino Cellular Shield
  VCC1 = 4 x AAA Battery Mount
  S1 = Toggle Switch [package=THT]

nets:
  N1: Part1.5V, VCC1.+, S1.L1
  N2: VCC1.-, S1.L2
