# Fritzing sketch 2_Switch (saved by Fritzing 0.8.7b)
breadboards: 1

parts:
  U1 = attiny85 [package=dip]
  S1 = Pushbutton [package="[THT]"]
  R1 = Resistor [tolerance=±5% resistance=1k package=THT]
  LED1 = LED - 5mm [color="Red (633nm)" package="5 mm [THT]"]
  R2 = Resistor [tolerance=±5% resistance=1k package=THT]
  VCC1 = prefix0000 [part_number=5V]

nets:
  N1: U1.Pin_4, R1.Pin_0, LED1.cathode, VCC1.connector1
  N2: U1.Pin_5, S1.Pin_2, R1.Pin_1
  N3: U1.Pin_6, R2.Pin_1
  N4: U1.Pin_8, S1.Pin_4
