# Fritzing sketch 3_PWM-anuduino (saved by Fritzing 0.8.7b)
breadboards: 1

parts:
  R1 = Resistor [tolerance=±5% resistance=220 package=THT]
  LED1 = LED - 5mm [color="Red (633nm)" package="5 mm [THT]"]
  VCC1 = 4 x AAA Battery Mount
  U1 = attiny85 [package=dip]
  U2 = POT [package=pot_alpha_rv16af-20]

nets:
  N1: R1.Pin_0, LED1.anode
  N2: R1.Pin_1, U1.Pin_6
  N3: LED1.cathode, VCC1.+, U1.Pin_4, U2.E
  N4: VCC1.-, U1.Pin_8, U2.A
  N5: U1.Pin_3, U2.S

custom parts:
  4 x AAA Battery Mount: A 4 x AAA battery pack (4.8 Volts with recharables)
