# Fritzing sketch 4_RGB-LED (saved by Fritzing 0.8.7b)
breadboards: 1

parts:
  R1 = Resistor [tolerance=±5% resistance=220 package=THT]
  R2 = Resistor [tolerance=±5% resistance=220 package=THT]
  R3 = Resistor [tolerance=±5% resistance=220 package=THT]
  U1 = attiny85 [package=dip]
  LED1 = RGB LED (com. anode, rbg) [package="5 mm [THT]"]
  VCC1 = 4 x AAA Battery Mount

nets:
  N1: R1.Pin_0, LED1.red_cathode
  N2: R1.Pin_1, U1.Pin_3
  N3: R2.Pin_0, LED1.blue_cathode
  N4: R2.Pin_1, U1.Pin_5
  N5: R3.Pin_0, LED1.green_cathode
  N6: R3.Pin_1, U1.Pin_6
  N7: U1.Pin_4, VCC1.+
  N8: U1.Pin_8, LED1.common_anode, VCC1.-

custom parts:
  4 x AAA Battery Mount: A 4 x AAA battery pack (4.8 Volts with recharables)
