# Fritzing sketch 5_Array-of-LEDs (saved by Fritzing 0.8.7b)
breadboards: 1

parts:
  U1 = attiny85 [package=dip]
  LED1 = LED - 5mm [color="Red (633nm)" package="5 mm [THT]"]
  LED2 = LED - 5mm [color="Red (633nm)" package="5 mm [THT]"]
  LED3 = LED - 5mm [color="Red (633nm)" package="5 mm [THT]"]
  LED4 = LED - 5mm [color="Red (633nm)" package="5 mm [THT]"]
  R1 = Resistor [tolerance=±5% resistance=220 package=THT]
  R2 = Resistor [tolerance=±5% resistance=220 package=THT]
  R3 = Resistor [tolerance=±5% resistance=220 package=THT]
  R4 = Resistor [tolerance=±5% resistance=220 package=THT]
  VCC1 = prefix0000

nets:
  N1: U1.Pin_2, R2.Pin_1
  N2: U1.Pin_3, R1.Pin_1
  N3: U1.Pin_4, LED1.cathode, LED2.cathode, LED3.cathode, LED4.cathode, VCC1.connector0
  N4: U1.Pin_5, R4.Pin_1
  N5: U1.Pin_6, R3.Pin_1
  N6: U1.Pin_8, VCC1.connector1
  N7: LED1.anode, R1.Pin_0
  N8: LED2.anode, R2.Pin_0
  N9: LED3.anode, R3.Pin_0
  N10: LED4.anode, R4.Pin_0
