# Fritzing sketch 6_LDR-anuduino (saved by Fritzing 0.8.7b)
breadboards: 1

parts:
  R1 = Photocell (LDR) [package=THT]
  R2 = Resistor [tolerance=±5% resistance=220 package=THT]
  R3 = Resistor [tolerance=±5% resistance=220 package=THT]
  LED1 = LED - 5mm [color="Red (633nm)" package="5 mm [THT]"]
  VCC1 = prefix0000
  U1 = attiny85 [package=dip]

nets:
  N1: R1.pin_0, R2.Pin_0, VCC1.connector0, U1.Pin_4
  N2: R1.pin_1, R3.Pin_0, U1.Pin_2
  N3: R2.Pin_1, LED1.anode
  N4: R3.Pin_1, VCC1.connector1, U1.Pin_8
  N5: LED1.cathode, U1.Pin_5
