# Fritzing sketch 7_PIR-sensor-anuduino (saved by Fritzing 0.8.7b)
breadboards: 1

parts:
  PIR1 = PIR sensor
  U1 = attiny85 [package=dip]
  VCC1 = 4 x AAA Battery Mount
  LED1 = LED - 5mm [color="Red (633nm)" package="5 mm [THT]"]
  R1 = Resistor [tolerance=±5% resistance=220 package=THT]

nets:
  N1: PIR1.VDD, U1.Pin_8, VCC1.-
  N2: PIR1.SIG, U1.Pin_6
  N3: PIR1.GND, U1.Pin_4, VCC1.+, LED1.cathode
  N4: U1.Pin_5, R1.Pin_0
  N5: LED1.anode, R1.Pin_1

custom parts:
  4 x AAA Battery Mount: A 4 x AAA battery pack (4.8 Volts with recharables)
