# Fritzing sketch 8_Music_Piezo-element (saved by Fritzing 0.8.7b)
breadboards: 1

parts:
  U1 = attiny85 [package=dip]
  VCC1 = 4 x AAA Battery Mount
  piezo_element = Buzzer 12mm [package=buzzer-ccv]

nets:
  N1: U1.Pin_4, VCC1.+, piezo_element.1
  N2: U1.Pin_5, piezo_element.2
  N3: U1.Pin_8, VCC1.-

custom parts:
  4 x AAA Battery Mount: A 4 x AAA battery pack (4.8 Volts with recharables)
