# Fritzing sketch 9_Steppermotor-Anuduino (saved by Fritzing 0.8.7b)
breadboards: 1

parts:
  J1 = Basic Servo
  U1 = attiny85 [package=dip]
  U2 = POT [package=pot_alpha_rv16af-20]
  VCC1 = 4 x AAA Battery Mount

nets:
  N1: J1.gnd, U1.Pin_4, U2.E, VCC1.+
  N2: J1.vcc, U1.Pin_8, U2.A, VCC1.-
  N3: J1.pulse, U1.Pin_5
  N4: U1.Pin_2, U2.S

custom parts:
  4 x AAA Battery Mount: A 4 x AAA battery pack (4.8 Volts with recharables)
