# Fritzing sketch LEDblink_1 (saved by Fritzing 0.8.7b)
breadboards: 1

parts:
  LED1 = LED - 5mm [color="Red (633nm)" package="5 mm [THT]"]
  R1 = Resistor [tolerance=±5% resistance=1k package=THT]
  U1 = attiny85 [package=dip]
  5V = 4 x AAA Battery Mount

nets:
  N1: LED1.cathode, U1.Pin_5
  N2: LED1.anode, R1.Pin_0
  N3: R1.Pin_1, U1.Pin_4, 5V.-
  N4: U1.Pin_8, 5V.+
