# Fritzing sketch Twisting-potentiometer (saved by Fritzing 0.8.7b)
breadboards: 1

parts:
  U1 = attiny85 [package=dip]
  U2 = POT [package=pot_mammoth]
  LED1 = LED - 5mm [color="Red (633nm)" package="5 mm [THT]"]
  V1 = DC Power [voltage=5]  # not connected
  R1 = Resistor [tolerance=±5% resistance=220 package=THT]
  VCC1 = 4 x AAA Battery Mount

nets (from the breadboard view):
  N1: U1.Pin_3, U2.A
  N2: U1.Pin_4, U2.E, LED1.cathode, VCC1.+
  N3: U1.Pin_6, R1.Pin_1
  N4: U1.Pin_8, U2.S, VCC1.-
  N5: LED1.anode, R1.Pin_0

custom parts:
  4 x AAA Battery Mount: A 4 x AAA battery pack (4.8 Volts with recharables)
